# Fritzing sketch ArduinoMicro_Toggleswitch_Fritzing (saved by Fritzing 0.9.6b)
circuit board: 2.90557cm x 5.98902cm

parts:
  Arduino = Arduino Micro (Rev3)
  Reset-Schalter = Pushbutton [package=THT]
  Umschalter = Taiway 100-SP-X-T1 SPDT Miniature Toggle Switch [part_number=100-SP-X-T1-0-0-B1-M2 package=THT]
  Schreibschutz = SPST Switch [package=switch-spdt_kit]

nets:
  N1: Arduino.GND, Reset-Schalter.leg0, Umschalter.COM
  N2: Arduino.D2/SDA, Umschalter.L1
  N3: Arduino.D3/SCL, Umschalter.L2
  N4: Arduino.RESET, Reset-Schalter.leg1
  N5: Arduino.A1, Schreibschutz.P
  N6: Arduino.A0, Schreibschutz.S
